# Fritzing sketch MPU6050 (saved by Fritzing 0.9.0b)

parts:
  GY1 = MPU-6050 Board GY-521 [form="♀ (female)" package=THT]
  Parte3 = Arduino Uno (Rev3)

nets:
  N1: GY1.pin1, Parte3.3V3
  N2: GY1.pin2, Parte3.GND
  N3: GY1.pin3, Parte3.A5/SCL
  N4: GY1.pin4, Parte3.A4/SDA

custom parts:
  MPU-6050 Board GY-521: Acelerometro y Giroscopio MPU-6050 Board GY-521
